# Fritzing sketch balakesh  (saved by Fritzing 0.9.4)
breadboards: 1

parts:
  Part1 = Arduino Uno (Rev3)
  LED1 = LED - 5mm [color="Red (633nm)" package="5 mm [THT]"]  # not connected
  LED2 = LED - 5mm [color="Red (633nm)" package="5 mm [THT]"]
  S1 = Pushbutton [package="[THT]"]
  R1 = Resistor [tolerance=±5% resistance=220 package=THT]
  R2 = Resistor [tolerance=±5% resistance=220 package=THT]

nets:
  N1: Part1.D8, S1.Pin_1, S1.Pin_2, R1.Pin_0
  N2: Part1.D13/SCK, R2.Pin_0
  N3: Part1.D2, LED2.cathode, R2.Pin_1
  N4: Part1.5V, R1.Pin_1
  N5: Part1.GND, LED2.anode, S1.Pin_3, S1.Pin_4

// code stored in the sketch: Untitled2.ino
int led = 13 ;
int led2 = 10 ;
void setup() {
pinMode(led,OUTPUT);
pinMode(led2,OUTPUT);
}
void loop ()
{
digitalWrite(led,HIGH);
delay(5000);
digitalWrite(led,LOW);
delay(5000);
digitalWrite(led2,HIGH);
delay(5000);
digitalWrite(led2,LOW);
delay(5000);
}
